// Logisim project u16a.circ as structural Verilog: 2 circuits, main circuit main
module main (
);

  wire ADDR_WRITE, and_4_out, ARG_0_STATIC, ARG_0_X_READ, ARG_0_X_WRITE, ARG_0_Y_READ, ARG_0_Y_WRITE,
       ARG_1_STATIC, ARG_1_X_READ, ARG_1_Y_READ, ARG_S_X_WRITE, ARG_S_Y_WRITE, ARG_STATIC, ARG_WRITE,
       BAX_WRITE, BAY_WRITE, BBX_WRITE, BBY_WRITE, BOX_WRITE, BOY_WRITE, BVX_WRITE, BVY_WRITE, CLK,
       demultiplexer_1_out5, INST_STEP_RESET, INST_WIDTH, INST_WRITE, INV_CLK, IP_COUNT, IP_READ, RAM_READ,
       xor_1_out, xor_2_out;
  wire [3:0] ARG_0, ARG_1, INST_STEP_q;
  wire [5:0] rom_1_data;
  wire [7:0] BAX_q, BAY_q, BBX_q, BBY_q, BOX_q, BOY_q, BVX_q, BVY_q, DATA_BUS, INST_q;
  wire [15:0] ADDR_q, IP_q, undriven;

  Counter #(.max('hffff), .width(16)) IP (
    .clr(1'b0), .load(1'b0), .up(1'b1), .count(IP_COUNT), .clk(CLK), .D(undriven), .Q(IP_q));  // open: carry
  Counter #(.max('hf), .width(4)) INST_STEP (
    .clr(INST_STEP_RESET), .load(1'b0), .up(1'b1), .count(1'b1), .clk(INV_CLK), .D(4'b0000), .Q(INST_STEP_q));  // open: carry
  Register INST (.D(DATA_BUS), .en(INST_WRITE), .clk(CLK), .Q(INST_q));  // open: clr
  Register #(.width(16)) ADDR (.D(IP_q), .en(ADDR_WRITE), .clk(CLK), .Q(ADDR_q));  // open: clr
  ROM #(.addrWidth(14)) rom_1 (
    .addr({INST_q, INST_STEP_q, ARG_STATIC, INST_WIDTH}), .data({INST_STEP_RESET, IP_COUNT, rom_1_data}));
  RAM #(.addrWidth(16), .asyncread("true"), .\type ("nonvolatile")) ram_1 (
    .addr(ADDR_q), .we(1'b0), .oe(1'b1), .clk(CLK), .din(DATA_BUS), .dout(DATA_BUS));
  Clock clock_1 (.out(CLK));
  not not_1 (INV_CLK, CLK);
  // Probe on {INST_STEP_RESET, IP_COUNT, rom_1_data}
  Demultiplexer #(.select(3)) demultiplexer_1 (
    .out1(ARG_0_X_READ), .out2(ARG_0_Y_READ), .out3(ARG_1_X_READ), .out4(ARG_1_Y_READ),
    .out5(demultiplexer_1_out5), .out6(RAM_READ), .out7(IP_READ), .in(1'b1), .sel(rom_1_data[2:0]));  // open: out0
  Demultiplexer #(.select(3)) demultiplexer_2 (
    .out1(ARG_0_X_WRITE), .out2(ARG_0_Y_WRITE), .out3(ARG_S_X_WRITE), .out4(ARG_S_Y_WRITE), .out5(ARG_WRITE),
    .out6(INST_WRITE), .out7(ADDR_WRITE), .in(1'b1), .sel(rom_1_data[5:3]));  // open: out0
  Register ARG (.D(DATA_BUS), .en(ARG_WRITE), .clk(CLK), .Q({ARG_1, ARG_0}));  // open: clr
  and and_1 (ARG_0_STATIC, ARG_0[0], ARG_0[1]);
  and and_2 (INST_WIDTH, ARG_0[2], ARG_0[3]);
  xor xor_1 (xor_1_out, ARG_0[2], ARG_0[3]);
  and and_3 (ARG_1_STATIC, ARG_1[0], ARG_1[1]);
  and and_4 (and_4_out, ARG_1[2], ARG_1[3]);
  xor xor_2 (xor_2_out, ARG_1[2], ARG_1[3]);
  Register BVX (.D(DATA_BUS), .en(BVX_WRITE), .clk(CLK), .Q(BVX_q));  // open: clr
  Register BVY (.D(DATA_BUS), .en(BVY_WRITE), .clk(CLK), .Q(BVY_q));  // open: clr
  LedBar ledbar_1 (
    .led0(BVX_q[7]), .led1(BVX_q[6]), .led2(BVX_q[5]), .led3(BVX_q[4]), .led4(BVX_q[3]), .led5(BVX_q[2]),
    .led6(BVX_q[1]), .led7(BVX_q[0]));
  LedBar ledbar_2 (
    .led0(BVY_q[7]), .led1(BVY_q[6]), .led2(BVY_q[5]), .led3(BVY_q[4]), .led4(BVY_q[3]), .led5(BVY_q[2]),
    .led6(BVY_q[1]), .led7(BVY_q[0]));
  Register BAX (.D(DATA_BUS), .en(BAX_WRITE), .clk(CLK), .Q(BAX_q));  // open: clr
  Register BAY (.D(DATA_BUS), .en(BAY_WRITE), .clk(CLK), .Q(BAY_q));  // open: clr
  or or_1 (ARG_STATIC, ARG_0_STATIC, ARG_1_STATIC);
  LedBar ledbar_3 (
    .led0(BAX_q[7]), .led1(BAX_q[6]), .led2(BAX_q[5]), .led3(BAX_q[4]), .led4(BAX_q[3]), .led5(BAX_q[2]),
    .led6(BAX_q[1]), .led7(BAX_q[0]));
  LedBar ledbar_4 (
    .led0(BAY_q[7]), .led1(BAY_q[6]), .led2(BAY_q[5]), .led3(BAY_q[4]), .led4(BAY_q[3]), .led5(BAY_q[2]),
    .led6(BAY_q[1]), .led7(BAY_q[0]));
  Register BBX (.D(DATA_BUS), .en(BBX_WRITE), .clk(CLK), .Q(BBX_q));  // open: clr
  Register BBY (.D(DATA_BUS), .en(BBY_WRITE), .clk(CLK), .Q(BBY_q));  // open: clr
  LedBar ledbar_5 (
    .led0(BBX_q[7]), .led1(BBX_q[6]), .led2(BBX_q[5]), .led3(BBX_q[4]), .led4(BBX_q[3]), .led5(BBX_q[2]),
    .led6(BBX_q[1]), .led7(BBX_q[0]));
  LedBar ledbar_6 (
    .led0(BBY_q[7]), .led1(BBY_q[6]), .led2(BBY_q[5]), .led3(BBY_q[4]), .led4(BBY_q[3]), .led5(BBY_q[2]),
    .led6(BBY_q[1]), .led7(BBY_q[0]));
  Register BOX (.D(DATA_BUS), .en(BOX_WRITE), .clk(CLK), .Q(BOX_q));  // open: clr
  Register BOY (.D(DATA_BUS), .en(BOY_WRITE), .clk(CLK), .Q(BOY_q));  // open: clr
  LedBar ledbar_7 (
    .led0(BOX_q[7]), .led1(BOX_q[6]), .led2(BOX_q[5]), .led3(BOX_q[4]), .led4(BOX_q[3]), .led5(BOX_q[2]),
    .led6(BOX_q[1]), .led7(BOX_q[0]));
  LedBar ledbar_8 (
    .led0(BOY_q[7]), .led1(BOY_q[6]), .led2(BOY_q[5]), .led3(BOY_q[4]), .led4(BOY_q[3]), .led5(BOY_q[2]),
    .led6(BOY_q[1]), .led7(BOY_q[0]));

  // Notes on the sheet:
  //   contents of rom_1 (hex, n*v repeats v):
  //   4*3f 4*76 4*80 52*0 4*3f 4*76 4*3f 4*2e 4*80
  //   Instruction Parsing
  //   TODO: Add arg_0_x etc
  //   Is word
  //   Is byte
  //   Is word
  //   Is byte
  //   Registers
endmodule

module ALU (
  input  zx,
  input  nx,
  input  f,
  input  no,
  input  [15:0] x,
  input  zy,
  input  nz,
  input  [15:0] y,
  output [15:0] o,
  output zr,
  output ng
);

  wire [15:0] adder_1_out, and_1_out, multiplexer_1_out, multiplexer_2_out, multiplexer_3_out,
       multiplexer_4_out, multiplexer_5_out, not_1_out, not_2_out, not_3_out;

  Multiplexer #(.width(16)) multiplexer_1 (.in0(x), .in1({16{1'b0}}), .out(multiplexer_1_out), .sel(zx));
  Multiplexer #(.width(16)) multiplexer_2 (.in0(y), .in1({16{1'b0}}), .out(multiplexer_2_out), .sel(zy));
  assign not_1_out = ~multiplexer_1_out;  // NOT_Gate not_1, 16 bits wide
  assign not_2_out = ~multiplexer_2_out;  // NOT_Gate not_2, 16 bits wide
  Multiplexer #(.width(16)) multiplexer_3 (.in0(multiplexer_1_out), .in1(not_1_out), .out(multiplexer_3_out), .sel(nx));
  Multiplexer #(.width(16)) multiplexer_4 (.in0(multiplexer_2_out), .in1(not_2_out), .out(multiplexer_4_out), .sel(nz));
  assign and_1_out = multiplexer_3_out & multiplexer_4_out;  // AND_Gate and_1, 16 bits wide
  Adder #(.width(16)) adder_1 (.a(multiplexer_3_out), .b(multiplexer_4_out), .out(adder_1_out));  // open: cin, cout
  and and_2 (zr, o[0], o[1], o[2], o[3], o[4], o[5], o[6], o[7], o[8], o[9], o[10], o[11], o[12], o[13], o[14], ng);
  Multiplexer #(.width(16)) multiplexer_5 (.in0(and_1_out), .in1(adder_1_out), .out(multiplexer_5_out), .sel(f));
  assign not_3_out = ~multiplexer_5_out;  // NOT_Gate not_3, 16 bits wide
  Multiplexer #(.width(16)) multiplexer_6 (.in0(multiplexer_5_out), .in1(not_3_out), .out({ng, o[14:0]}), .sel(no));

  assign o[15] = ng;
endmodule
